# Fritzing sketch fritzing-planter-schematics (saved by Fritzing 0.9.3b)
breadboards: 1

parts:
  Raspberry_Pi_1 = Raspberry Pi 3 [part_number=RPI-3-V1.2]
  RHT1 = Humidity and Temperature Sensor RHT03
  RHT2 = Humidity and Temperature Sensor RHT03
  Bauteil1 = Soil Moisture Sensor
  Bauteil3 = BH1750  # not connected
  R1 = Resistor [tolerance=±5% resistance=220 package="2010 [SMD]"]
  R2 = Resistor [tolerance=±5% resistance=220 package="2010 [SMD]"]
  R3 = Resistor [tolerance=±5% resistance=220 package="2010 [SMD]"]
  R4 = Resistor [tolerance=±5% resistance=220 package="2010 [SMD]"]

nets:
  GND: Raspberry_Pi_1.GND, RHT1.GND_2, RHT2.GND_2, Bauteil1.GND
  N1: Raspberry_Pi_1.GPIO27, R3.Pin_0
  VCC: Raspberry_Pi_1.GPIO22, Raspberry_Pi_1.3V3, RHT1.Vcc, RHT2.Vcc, Bauteil1.VCC, R4.Pin_0
  N2: Raspberry_Pi_1.GPIO24, R1.Pin_0
  N3: Raspberry_Pi_1.GPIO23, R2.Pin_0
  N4: RHT1.Data-signal, R1.Pin_1
  N5: RHT2.Data-signal, R2.Pin_1
  N6: Bauteil1.SIG, R3.Pin_1

custom parts:
  BH1750: Light Sensor
